// Digital circuit Tarea_Sumador_Registro de corrimiento.dig as structural Verilog
module Tarea_Sumador_Registro_de_corrimiento (
  input  clk,
  input  X3,
  input  X2,
  input  X1,
  input  X0,
  input  ADD_SUB,
  input  C,
  input  D,
  input  C_2,
  input  D_2,
  output Q3,
  output Q2,
  output Q1,
  output Q0,
  output Q3_2,
  output Q2_2,
  output Q1_2,
  output Q0_2
);

  wire add_1_s, add_2_c_o, add_2_s, add_3_c_o, add_3_s, add_4_c_o, add_4_s, d_ff_1_q, d_ff_2_q, d_ff_3_q,
       d_ff_4_q, d_ff_5_q, d_ff_6_q, d_ff_9_q, d_ff_10_q, d_ff_13_q, d_ff_14_q, d_ff_17_q, d_ff_19_q,
       not_1_out, not_2_out, not_3_out, not_4_out, not_5_out, not_6_out, not_7_out, not_8_out, xor_1_out,
       xor_2_out, xor_3_out, xor_4_out;

  xor xor_1 (xor_1_out, X3, ADD_SUB);
  xor xor_2 (xor_2_out, X2, ADD_SUB);
  xor xor_3 (xor_3_out, X1, ADD_SUB);
  xor xor_4 (xor_4_out, X0, ADD_SUB);
  Add add_1 (.a(d_ff_1_q), .b(xor_1_out), .c_i(add_2_c_o), .s(add_1_s));  // open: c_o
  Add add_2 (.a(d_ff_2_q), .b(xor_2_out), .c_i(add_3_c_o), .s(add_2_s), .c_o(add_2_c_o));
  Add add_3 (.a(d_ff_3_q), .b(xor_3_out), .c_i(add_4_c_o), .s(add_3_s), .c_o(add_3_c_o));
  Add add_4 (.a(d_ff_4_q), .b(xor_4_out), .c_i(ADD_SUB), .s(add_4_s), .c_o(add_4_c_o));
  D_FF d_ff_1 (.D(add_1_s), .C(clk), .Q(d_ff_1_q));  // open: nQ
  D_FF d_ff_2 (.D(add_2_s), .C(clk), .Q(d_ff_2_q));  // open: nQ
  D_FF d_ff_3 (.D(add_3_s), .C(clk), .Q(d_ff_3_q));  // open: nQ
  D_FF d_ff_4 (.D(add_4_s), .C(clk), .Q(d_ff_4_q));  // open: nQ
  LED led_1 (.in(d_ff_1_q));
  LED led_2 (.in(d_ff_2_q));
  LED led_3 (.in(d_ff_3_q));
  LED led_4 (.in(d_ff_4_q));
  not not_1 (not_1_out, C);
  D_FF d_ff_5 (.D(Q2_2), .C(C_2), .Q(d_ff_5_q));  // open: nQ
  D_FF d_ff_6 (.D(D), .C(not_1_out), .Q(d_ff_6_q));  // open: nQ
  not not_2 (not_2_out, C_2);
  D_FF d_ff_7 (.D(d_ff_6_q), .C(C), .Q(Q3));  // open: nQ
  D_FF d_ff_8 (.D(d_ff_5_q), .C(not_2_out), .Q(Q3_2));  // open: nQ
  not not_3 (not_3_out, C);
  D_FF d_ff_9 (.D(Q3), .C(not_3_out), .Q(d_ff_9_q));  // open: nQ
  D_FF d_ff_10 (.D(Q1_2), .C(C_2), .Q(d_ff_10_q));  // open: nQ
  D_FF d_ff_11 (.D(d_ff_9_q), .C(C), .Q(Q2));  // open: nQ
  not not_4 (not_4_out, C_2);
  D_FF d_ff_12 (.D(d_ff_10_q), .C(not_4_out), .Q(Q2_2));  // open: nQ
  not not_5 (not_5_out, C);
  D_FF d_ff_13 (.D(Q2), .C(not_5_out), .Q(d_ff_13_q));  // open: nQ
  D_FF d_ff_14 (.D(Q0_2), .C(C_2), .Q(d_ff_14_q));  // open: nQ
  D_FF d_ff_15 (.D(d_ff_13_q), .C(C), .Q(Q1));  // open: nQ
  not not_6 (not_6_out, C_2);
  not not_7 (not_7_out, C);
  D_FF d_ff_16 (.D(d_ff_14_q), .C(not_6_out), .Q(Q1_2));  // open: nQ
  D_FF d_ff_17 (.D(Q1), .C(not_7_out), .Q(d_ff_17_q));  // open: nQ
  D_FF d_ff_18 (.D(d_ff_17_q), .C(C), .Q(Q0));  // open: nQ
  D_FF d_ff_19 (.D(D_2), .C(C_2), .Q(d_ff_19_q));  // open: nQ
  not not_8 (not_8_out, C_2);
  D_FF d_ff_20 (.D(d_ff_19_q), .C(not_8_out), .Q(Q0_2));  // open: nQ

  // Notes on the sheet:
  //   Sumador / Restador complemento a dos
  //   RSR Registro de corrimiento a la derecha
  //   LSR Registro de corrimiento a la derecha
endmodule
